# Fritzing sketch gotimer (saved by Fritzing 0.9.3b)
breadboards: 1

parts:
  R2 = Resistor [tolerance=±5% resistance=220 package=THT]
  Pi_Pico = Raspberry Pi Pico
  R1 = Resistor [tolerance=±5% resistance=220 package=THT]
  R6 = Resistor [tolerance=±5% resistance=220 package=THT]
  R7 = Resistor [tolerance=±5% resistance=220 package=THT]
  R4 = Resistor [tolerance=±5% resistance=220 package=THT]
  R10 = Resistor [tolerance=±5% resistance=220 package=THT]
  R5 = Resistor [tolerance=±5% resistance=220 package=THT]
  7-Seg_LED_x4 = 7-SEGMENT-4DIGIT-YOUNGSUN [package=7-segment-4digit-youngsun-longpads]
  S1 = Pushbutton [package="[THT]"]

nets:
  N1: R2.Pin_0, Pi_Pico.pin_17
  N2: R2.Pin_1, 7-Seg_LED_x4.E
  N3: Pi_Pico.pin_3, Pi_Pico.pin_8, Pi_Pico.pin_13, Pi_Pico.pin_18, Pi_Pico.pin_23, Pi_Pico.pin_28, Pi_Pico.pin_33, Pi_Pico.pin_38
  N4: Pi_Pico.pin_12, S1.Pin_3, S1.Pin_4
  N5: Pi_Pico.pin_19, R1.Pin_0
  N6: Pi_Pico.pin_20, R10.Pin_0
  N7: Pi_Pico.pin_21, R6.Pin_0
  N8: Pi_Pico.pin_22, R7.Pin_1
  N9: Pi_Pico.pin_24, R4.Pin_1
  N10: Pi_Pico.pin_25, R5.Pin_0
  N11: Pi_Pico.pin_36, S1.Pin_1, S1.Pin_2
  N12: R1.Pin_1, 7-Seg_LED_x4.D
  N13: R6.Pin_1, 7-Seg_LED_x4.B
  N14: R7.Pin_0, 7-Seg_LED_x4.C
  N15: R4.Pin_0, 7-Seg_LED_x4.F
  N16: R10.Pin_1, 7-Seg_LED_x4.A
  N17: R5.Pin_1, 7-Seg_LED_x4.G

notes:
  D Nisbet 2021

custom parts:
  Raspberry Pi Pico: Raspberry Pi Pico. Based around the RP2040 microcontroller the Pico is a low cost microcontroller device bringing Raspberry Pi quality, cost, and easy of use to the microcontroller space. Jan 2021, Split part in to two versions: tht (this one) and SMD. This one will drill holes for a .1 in header in pcb to allow plugging in the module as well as providing pads to solder the module to the top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

// code stored in the sketch: countup.ino
from machine import Pin
import time
import utime

t=0.2
#  _ - a
# |_|- f,g,b
# |_|- e,d,c


a=Pin(15, Pin.OUT)
b=Pin(16, Pin.OUT)
c=Pin(17, Pin.OUT)
d=Pin(14, Pin.OUT)
e=Pin(13, Pin.OUT)
f=Pin(18, Pin.OUT)
g=Pin(19, Pin.OUT)

digits = (12,11,10,9)
digits = (9,10,11,12)

#for i in range(0,4):
# di=(Pin(digits[i], Pin.OUT))
# di.on()
def dig1():
    di=Pin(digits[0], Pin.OUT,0)
def dig2():
    di=Pin(digits[1], Pin.OUT,0)
def dig3():
    di=Pin(digits[2], Pin.OUT,0)
def dig4():
    di=Pin(digits[3], Pin.OUT,0)
def reset(i):
        di=(Pin(digits[i], Pin.OUT,0))

segments = (15,16,17,14,13,18,19)

num = {' ':(1,1,1,1,1,1,1),
    '0':(0,0,0,0,0,0,1),
    '1':(1,0,0,1,1,1,1),
    '2':(0,0,1,0,0,1,0),
    '3':(0,0,0,0,1,1,0),
    '4':(1,0,0,1,1,0,0),
    '5':(0,1,0,0,1,0,0),
    '6':(0,1,0,0,0,0,0),
    '7':(0,0,0,1,1,1,1),
    '8':(0,0,0,0,0,0,0),
    '9':(0,0,0,0,1,0,0)}

def zero():
    a.off()
    b.off()
    c.off()
    d.off()
    e.off()
    f.off()
    g.on()

def one():
    a.on()
    b.off()
    c.off()
    d.on()
    e.on()
    f.on()
    g.on()

def two():
    a.off()
    b.off()
    c.on()
    d.off()
    e.off()
    f.on()
    g.off()
    
def three():
    f.on()
    e.on()
    a.off()
    b.off()
    c.off()
    d.off()
    g.off()
    
def four():
    a.on()
    e.on()
    d.on()
    b.off()
    c.off()
    f.off()
    g.off()
    
def five():
    b.on()
    e.on()
    a.off()
    c.off()
    d.off()
    f.off()
    g.off()
    
def six():
    b.on()
    a.off()
    c.off()
    d.off()
    e.off()
    f.off()
    g.off()

def seven():
    e.on()
    f.on()
    g.on()
    a.off()
    b.off()
    c.off()
    d.on()

def eight():
    a.off()
    b.off()
    c.off()
    d.off()
    e.off()
    f.off()
    g.off()

def nine():
    e.on()
    d.on()
    a.off()
    b.off()
    c.off()
    f.off()
    g.off()

def space():
    e.on()
    d.on()
    a.on()
    b.on()
    c.on()
    f.on()
    g.on()
    
def count(t):
    one()
    time.sleep(t)
    two()
    time.sleep(t)
    three()
    time.sleep(t)
    four()
    time.sleep(t)
    five()
    time.sleep(t)
    six()
    time.sleep(t)
    seven()
    time.sleep(t)
    eight()
    time.sleep(t)
    nine()
    time.sleep(t)
    zero()
    time.sleep(t)
no=1
#(year, month, mday, hour, minute, second, weekday, yearday)
while True:
 #n=time.gmtime()

 #num=n[0]

 s="% 4s" % str(no)
 space()
 for digit in range(0,4):
        for loop in range(0,7):
            #print (digits[digit],segments[loop],num[s[digit]][loop])
            place=Pin(digits[digit], Pin.OUT, value=1)
            show=Pin(segments[loop], Pin.OUT, value=num[s[digit]][loop])

        disp=Pin(digits[digit], Pin.OUT, value=1)
        time.sleep(0.003)
        disp=Pin(digits[digit], Pin.OUT, value=0)
        if (no==9999):
            no=1
        else:
            no=no+1
