# Fritzing sketch temp_pres_show (saved by Fritzing 0.9.3b)
circuit board: 8.46667cm x 5.64444cm
breadboards: 2

parts:
  Pico = Raspberry Pi Pico
  LED1 = 7-SEGMENT-4DIGIT-YOUNGSUN [package=7-segment-4digit-youngsun]
  R1 = Resistor [tolerance=±5% resistance=220 package=THT]
  R2 = Resistor [tolerance=±5% resistance=220 package=THT]
  R3 = Resistor [tolerance=±5% resistance=220 package=THT]
  R4 = Resistor [tolerance=±5% resistance=220 package=THT]
  R5 = Resistor [tolerance=±5% resistance=220 package=THT]
  R6 = Resistor [tolerance=±5% resistance=220 package=THT]
  R7 = Resistor [tolerance=±5% resistance=220 package=THT]
  R8 = Resistor [tolerance=±5% resistance=220 package=THT]
  BME280_Sensor = BME280 Breakout

nets:
  N1: Pico.pin_3, Pico.pin_8, Pico.pin_13, Pico.pin_18, Pico.pin_23, Pico.pin_28, Pico.pin_33, Pico.pin_38, Pico.pin_42, BME280_Sensor.GND
  N2: Pico.pin_4, LED1.DIG1
  N3: Pico.pin_5, LED1.DIG2
  N4: Pico.pin_6, LED1.DIG3
  N5: Pico.pin_7, LED1.DIG4
  N6: Pico.pin_14, LED1.B, R2.Pin_0, R2.Pin_1
  N7: Pico.pin_15, LED1.E, R5.Pin_0, R5.Pin_1
  N8: Pico.pin_16, LED1.D, R4.Pin_0, R4.Pin_1
  N9: Pico.pin_17, LED1.F, R6.Pin_0, R6.Pin_1
  N10: Pico.pin_19, LED1.A, R1.Pin_0, R1.Pin_1
  N11: Pico.pin_21, R7.Pin_0
  N12: Pico.pin_25, LED1.C, R3.Pin_0, R3.Pin_1
  N13: Pico.pin_27, LED1.DP, R8.Pin_0, R8.Pin_1
  N14: LED1.G, R7.Pin_1

custom parts:
  Raspberry Pi Pico: Raspberry Pi Pico. Based around the RP2040 microcontroller the Pico is a low cost microcontroller device bringing Raspberry Pi quality, cost, and easy of use to the microcontroller space. Jan 2021, Split part in to two versions: tht (this one) and SMD. This one will drill holes for a .1 in header in pcb to allow plugging in the module as well as providing pads to solder the module to the top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

// code stored in the sketch: temp_pres_show.ino
from machine import Pin
import time
import utime
from bme280 import *
from machine import I2C

#  _ - a
# |_|- f,g,b
# |_|- e,d,c

"""
Refactored code as setting the temp variable can't happen every led refresh loop as it switches it off for too long.
So only get a new sensor reading every 50 `ticks` and display that.
Put the display code in it's own function too.
"""

num = {' ':(1,1,1,1,1,1,1),
    '0':(0,0,0,0,0,0,1),
    '1':(1,0,0,1,1,1,1),
    '2':(0,0,1,0,0,1,0),
    '3':(0,0,0,0,1,1,0),
    '4':(1,0,0,1,1,0,0),
    '5':(0,1,0,0,1,0,0),
    '6':(0,1,0,0,0,0,0),
    '7':(0,0,0,1,1,1,1),
    '8':(0,0,0,0,0,0,0),
    '9':(0,0,0,0,1,0,0),
    'c':(1,1,1,0,0,1,0)}


#  _ - a
# |_|- f,g,b
# |_|- e,d,c

# - 14 a GP14
# - 16 b GP10
# - 13 c GP19
# - 3  d GP12
# - 5  e GP11
# - 11 f GP13
# - 15 g GP9
# - 7  dp GP21
segs=(14,10,19,12,11,13,9,16)
segments=segs
the_segs=('a','b','c','d','e','f','g','dec')

digits = (2,3,4,5)
no=1234


sda=Pin(0)
scl=Pin(1)


#ds = ds1302.DS1302(clk_pin,data_pin,ce_pin)
i2c = I2C(0, sda=sda, scl=scl, freq=400000)
width=2
bme280 = BME280(i2c=i2c)

def show_number(val):
    digits=[0,0,0]
    abs_val = abs(val)
    temp_val = abs_val



def seg(display_string,count=1):
    display_string="% 4s" % str(display_string)
    for digit in (0,2,1,3):
        for loop in range(7):
          place=Pin(digits[digit], Pin.OUT, value=0)
          if digit == 1:
              decimal=Pin(segs[7],Pin.OUT,value=0)
          else: decimal=Pin(segs[7],Pin.OUT,value=1)
          
          show=Pin(segs[loop], Pin.OUT, value=num[display_string[digit]][loop])
        disp=Pin(digits[digit], Pin.OUT, value=1)
        time.sleep(0.001)
        disp=Pin(digits[digit], Pin.OUT, value=0)

def seg(display_string,kind):
    for digit in (0,2,3,1):
        for loop in range(0,7):
          place=Pin(digits[digit], Pin.OUT, value=0)
          if digit == 1 and kind=='temp':
              decimal=Pin(segs[7],Pin.OUT,value=0)
          else: decimal=Pin(segs[7],Pin.OUT,value=1)
          #print (loop)
          #print(num[display_string[digit]][loop])
          show=Pin(segments[loop], Pin.OUT, value=num[display_string[digit]][loop])
          #time.sleep(0.01)
        disp=Pin(digits[digit], Pin.OUT, value=1)
        time.sleep(0.002)
        disp=Pin(digits[digit], Pin.OUT, value=0)



t= '{:.0f}'.format(bme280.read_compensated_data()[0] / 10)


p= '{:4d}'.format(int(bme280.read_compensated_data()[1] / 256 / 100))
#p= int(bme280.read_compensated_data()[1] / 256 / 100)
i=0
while True:
    i=0
    t_end = time.time() + 10
    
    while time.time() < t_end:
        t= '{:.0f}'.format(bme280.read_compensated_data()[0] / 10)
        t_end_2 = time.time() + 1
        while time.time() < t_end_2:
            seg(t+'c','temp')

    t_end = time.time() + 10
    p= '{:4d}'.format(int(bme280.read_compensated_data()[1] / 256 / 100))
    while time.time() < t_end:
        seg(str(p),'pres')
        i+=1

// code stored in the sketch: temp_pres_show.py.ino
from machine import Pin
import time
import utime
from bme280 import *
from machine import I2C

#  _ - a
# |_|- f,g,b
# |_|- e,d,c

"""
Refactored code as setting the temp variable can't happen every led refresh loop as it switches it off for too long.
So only get a new sensor reading every 50 `ticks` and display that.
Put the display code in it's own function too.
"""

num = {' ':(1,1,1,1,1,1,1),
    '0':(0,0,0,0,0,0,1),
    '1':(1,0,0,1,1,1,1),
    '2':(0,0,1,0,0,1,0),
    '3':(0,0,0,0,1,1,0),
    '4':(1,0,0,1,1,0,0),
    '5':(0,1,0,0,1,0,0),
    '6':(0,1,0,0,0,0,0),
    '7':(0,0,0,1,1,1,1),
    '8':(0,0,0,0,0,0,0),
    '9':(0,0,0,0,1,0,0),
    'c':(1,1,1,0,0,1,0)}


#  _ - a
# |_|- f,g,b
# |_|- e,d,c

# - 14 a GP14
# - 16 b GP10
# - 13 c GP19
# - 3  d GP12
# - 5  e GP11
# - 11 f GP13
# - 15 g GP9
# - 7  dp GP21
segs=(14,10,19,12,11,13,9,16)
segments=segs
the_segs=('a','b','c','d','e','f','g','dec')

digits = (2,3,4,5)
no=1234


sda=Pin(0)
scl=Pin(1)


#ds = ds1302.DS1302(clk_pin,data_pin,ce_pin)
i2c = I2C(0, sda=sda, scl=scl, freq=400000)
width=2
bme280 = BME280(i2c=i2c)

def show_number(val):
    digits=[0,0,0]
    abs_val = abs(val)
    temp_val = abs_val



def seg(display_string,count=1):
    display_string="% 4s" % str(display_string)
    for digit in (0,2,1,3):
        for loop in range(7):
          place=Pin(digits[digit], Pin.OUT, value=0)
          if digit == 1:
              decimal=Pin(segs[7],Pin.OUT,value=0)
          else: decimal=Pin(segs[7],Pin.OUT,value=1)
          
          show=Pin(segs[loop], Pin.OUT, value=num[display_string[digit]][loop])
        disp=Pin(digits[digit], Pin.OUT, value=1)
        time.sleep(0.001)
        disp=Pin(digits[digit], Pin.OUT, value=0)

def seg(display_string,kind):
    for digit in (0,2,3,1):
        for loop in range(0,7):
          place=Pin(digits[digit], Pin.OUT, value=0)
          if digit == 1 and kind=='temp':
              decimal=Pin(segs[7],Pin.OUT,value=0)
          else: decimal=Pin(segs[7],Pin.OUT,value=1)
          #print (loop)
          #print(num[display_string[digit]][loop])
          show=Pin(segments[loop], Pin.OUT, value=num[display_string[digit]][loop])
          #time.sleep(0.01)
        disp=Pin(digits[digit], Pin.OUT, value=1)
        time.sleep(0.002)
        disp=Pin(digits[digit], Pin.OUT, value=0)



t= '{:.0f}'.format(bme280.read_compensated_data()[0] / 10)


p= '{:4d}'.format(int(bme280.read_compensated_data()[1] / 256 / 100))
#p= int(bme280.read_compensated_data()[1] / 256 / 100)
i=0
while True:
    i=0
    t_end = time.time() + 10
    
    while time.time() < t_end:
        t= '{:.0f}'.format(bme280.read_compensated_data()[0] / 10)
        t_end_2 = time.time() + 1
        while time.time() < t_end_2:
            seg(t+'c','temp')

    t_end = time.time() + 10
    p= '{:4d}'.format(int(bme280.read_compensated_data()[1] / 256 / 100))
    while time.time() < t_end:
        seg(str(p),'pres')
        i+=1
